# Fritzing sketch câblage (saved by Fritzing 0.9.3b)
breadboards: 1

parts:
  Yun = Arduino Yun
  S1 = PH meter [package=THT]
  ORP = ORP meter [package=THT]
  Niveau_eau_local = Soil Moisture Sensor
  Grove1 = Grove OLED 128x96
  DS1 = DS18B20 1-Wire Temperature Sensor [part_number=DS18B20]
  R1 = Resistor [tolerance=±5% resistance=220 package="1206 [SMD]"]
  J1 = Piezo Speaker
  DHT1 = DHT11 Humitidy and Temperature Sensor  # not connected

nets (from the breadboard view):
  N1: Yun.A0, S1.pin1
  N2: Yun.A1, ORP.pin1
  N3: Yun.A2, Niveau_eau_local.SIG
  5V: Yun.5V, S1.pin2, ORP.pin2, Niveau_eau_local.VCC, DS1.VDD, R1.Pin_0
  GND: Yun.GND, S1.pin3, ORP.pin3, Niveau_eau_local.GND, Grove1.GND, DS1.GND, J1.pin1
  N4: Yun.D2/SDA, Yun.D2, Grove1.SDA, J1.pin2
  N5: Yun.D3/SCL, Yun.D3_PWM, Grove1.SCL
  N6: Yun.D6_PWM, R1.Pin_1
  3V3: Yun.3V3, Grove1.VCC

custom parts:
  ORP meter: DFrobot ORP meter (SKU SEN0161)
  DHT11 Humitidy and Temperature Sensor: DHT11 Humidity and Temperature Sensor
